# Fritzing sketch arduino-nRF8001 (saved by Fritzing 0.8.7b)
circuit board: 8.46667cm x 5.64444cm

parts:
  RF1 = nRF8001 Bluetooth LE Breakout
  Part1 = Arduino Pro Mini v13
  T1 = LM35 Temperature Sensor [package="TO92 [THT]"]
  VCC1 = Battery block 9V

nets:
  N1: RF1.SCK, Part1.D13/SCK
  N2: RF1.MISO, Part1.D12/MISO
  N3: RF1.MOSI, Part1.D11_PWM/MOSI
  N4: RF1.REQ, Part1.D10_PWM/SS
  N5: RF1.RDY, Part1.D2
  N6: RF1.RST, Part1.D9_PWM
  GND: RF1.GND, Part1.GND, T1.GND, VCC1.-
  VIN: RF1.VIN, Part1.VCC, T1.+Vs
  N7: Part1.RAW, VCC1.+
  N8: Part1.A0, T1.Vout

custom parts:
  nRF8001 Bluetooth LE Breakout: nRF8001 Breakout Board
